# Fritzing sketch Alarm_Clock_Circuit_Diagram (saved by Fritzing 0.9.4)
breadboards: 1

parts:
  Part1 = Arduino Uno (Rev3)
  LCD1 = LCD screen
  S1 = Pushbutton [package="[THT]"]
  S2 = Pushbutton [package="[THT]"]
  R1 = Trimmer Potentiometer [maximum_resistance=10kΩ package=THT]
  R2 = Resistor [tolerance=±5% resistance=10k package=THT]
  R3 = Resistor [tolerance=±1% resistance=220 package=THT]
  Q1 = PNP-Transistor [package="TO92 [THT]"]
  R4 = Photocell (LDR) [package=THT]
  R5 = Resistor [tolerance=±5% resistance=10k package=THT]

nets:
  N1: Part1.A5/SCL, R4.pin_1, R5.Pin_1
  N2: Part1.D8, S1.Pin_3, S1.Pin_4
  N3: Part1.D9_PWM, S2.Pin_3, S2.Pin_4
  N4: Part1.D11_PWM/MOSI, LCD1.E
  N5: Part1.D12/MISO, LCD1.RS
  GND: Part1.GND, LCD1.VSS, LCD1.R/W, S1.Pin_1, S1.Pin_2, S2.Pin_1, S2.Pin_2, R1.leg1, Q1.C, R4.pin_0
  N6: Part1.D2, LCD1.DB7
  N7: Part1.D3_PWM, LCD1.DB6
  N8: Part1.D4, LCD1.DB5
  N9: Part1.D5_PWM, LCD1.DB4
  N10: Part1.D6_PWM, R2.Pin_0
  5V: Part1.5V, LCD1.VDD, R1.leg2, R3.Pin_0, R5.Pin_0
  N11: LCD1.V0, R1.wiper
  N12: LCD1.LED+, R3.Pin_1
  N13: LCD1.LED-, Q1.E
  N14: R2.Pin_1, Q1.B
